// Logisim project control_logic.circ as structural Verilog: 2 circuits, main circuit control_logic
module control_logic (
  input  [31:0] instIF,
  input  [31:0] instID,
  input  [31:0] instEX,
  input  [31:0] instMem,
  input  [31:0] instWb,
  input  BrEq,
  input  BrLt,
  output PCSel,
  output RegWEn,
  output [2:0] ImmSel,
  output [1:0] raSel,
  output [1:0] spSel,
  output [1:0] t0Sel,
  output [1:0] t1Sel,
  output [1:0] t2Sel,
  output [1:0] s0Sel,
  output [1:0] s1Sel,
  output [1:0] a0Sel,
  output [1:0] rs1Sel,
  output [1:0] rs2Sel,
  output BrUn,
  output ASel,
  output BSel,
  output [3:0] ALUSel,
  output MemRW,
  output [3:0] WRITE_ENABLE,
  output [1:0] WBSel,
  output [1:0] WBSelMem,
  output CSRSel,
  output CSRWen
);

  wire and_1_out, and_2_out, and_3_out, and_4_out, and_6_out, and_8_out, and_9_out, and_10_out, and_12_out,
       comparator_1_eq, comparator_2_eq, not_1_out, not_2_out, not_3_out, not_4_out, not_5_out, not_6_out,
       not_7_out, not_8_out, not_9_out, not_10_out, not_11_out, not_13_out, not_14_out, not_15_out,
       not_16_out, or_1_out, or_3_out, xor_1_out, xor_2_out, xor_3_out;
  wire [1:0] bit_extender_4_out, bit_extender_5_out, rs1Hazard_out_5, rs2Hazrd_out_5;
  wire [3:0] bit_extender_2_out, bit_extender_3_out, multiplexer_1_out, multiplexer_4_out;
  wire [4:0] adder_1_out, and_7_out, bit_extender_1_out;

  not not_1 (not_1_out, instEX[2]);
  assign bit_extender_1_out = {{4{not_1_out}}, not_1_out};  // Bit_Extender bit_extender_1
  Adder #(.width(5)) adder_1 (
    .a({instEX[30], instEX[25], instEX[14:12]}), .b(5'b00001), .out(adder_1_out));  // open: cin, cout
  not not_2 (not_2_out, instEX[4]);
  and and_1 (and_1_out, instEX[2], not_2_out, instEX[5], instEX[6]);
  not not_3 (not_3_out, instEX[2]);
  not not_4 (not_4_out, instEX[4]);
  and and_2 (and_2_out, not_3_out, not_4_out, instEX[5], instEX[6]);
  xor xor_1 (xor_1_out, BrEq, instEX[12]);
  not not_5 (not_5_out, instEX[13]);
  not not_6 (not_6_out, instEX[14]);
  xor xor_2 (xor_2_out, instEX[12], BrLt);
  not not_7 (not_7_out, instWb[2]);
  not not_8 (not_8_out, instWb[4]);
  and and_3 (and_3_out, xor_1_out, not_5_out, not_6_out);
  and and_4 (and_4_out, instEX[14], xor_2_out);
  not not_9 (not_9_out, instWb[6]);
  and and_5 (BrUn, instEX[13], instEX[14]);
  xor xor_3 (xor_3_out, instEX[2], instEX[6]);
  not not_10 (not_10_out, instEX[4]);
  not not_11 (not_11_out, instEX[5]);
  and and_6 (and_6_out, instEX[4], instEX[5]);
  assign and_7_out = bit_extender_1_out & adder_1_out;  // AND_Gate and_7, 5 bits wide
  or or_1 (or_1_out, and_3_out, and_4_out);
  and and_8 (and_8_out, instWb[0], instWb[1], not_7_out);
  and and_9 (and_9_out, not_8_out, instWb[5], not_9_out);
  or or_2 (BSel, instEX[2], not_10_out, not_11_out);
  assign bit_extender_2_out = {{3{and_6_out}}, and_6_out};  // Bit_Extender bit_extender_2
  Multiplexer #(.enable("false"), .select(5), .width(4)) multiplexer_1 (
    .in0(4'b1101), .in1(4'b0000), .in2(4'b0110), .in3(4'b0111), .in5(4'b0011), .in6(4'b0100), .in7(4'b0010),
    .in8(4'b0001), .in9(4'b1010), .in10(4'b1110), .in12(4'b1011), .in17(4'b1100), .in22(4'b0101),
    .out(multiplexer_1_out), .sel(and_7_out));  // open: in4, in11, in13, in14, in15, in16, in18, in19, in20, in21, in23, in24, in25, in26, in27, in28, in29, in30, in31
  and and_10 (and_10_out, and_2_out, or_1_out);
  or or_3 (or_3_out, and_9_out, instWb[6]);
  Multiplexer #(.enable("false"), .select(5), .width(3)) multiplexer_2 (
    .in0(3'b000), .in4(3'b000), .in5(3'b011), .in8(3'b001), .in13(3'b011), .in24(3'b010), .in25(3'b000),
    .in27(3'b100), .in28(3'b101), .out(ImmSel), .sel(instID[6:2]));  // open: in1, in2, in3, in6, in7, in9, in10, in11, in12, in14, in15, in16, in17, in18, in19, in20, in21, in22, in23, in26, in29, in30, in31
  or or_4 (ASel, xor_3_out, instEX[3]);
  assign ALUSel = bit_extender_2_out & multiplexer_1_out;  // AND_Gate and_11, 4 bits wide
  or or_5 (PCSel, and_1_out, and_10_out);
  not not_12 (RegWEn, and_12_out);
  and and_12 (and_12_out, and_8_out, or_3_out);
  not not_13 (not_13_out, instMem[4]);
  not not_14 (not_14_out, instMem[6]);
  assign bit_extender_3_out = {{3{MemRW}}, MemRW};  // Bit_Extender bit_extender_3
  Comparator #(.width(5)) comparator_1 (.a({5{1'b0}}), .b(instID[19:15]), .eq(comparator_1_eq));  // open: gt, lt
  Comparator #(.width(5)) comparator_2 (.a({5{1'b0}}), .b(instID[24:20]), .eq(comparator_2_eq));  // open: gt, lt
  and and_13 (MemRW, not_13_out, instMem[5], not_14_out);
  Multiplexer #(.enable("false"), .select(3), .width(2)) multiplexer_3 (
    .in0(2'b01), .in1(2'b00), .in3(2'b00), .in6(2'b10), .out(WBSel), .sel(instWb[6:4]));  // open: in2, in4, in5, in7
  and and_14 (CSRWen, instID[4], instID[5], instID[6]);
  Multiplexer #(.enable("false"), .select(2), .width(4)) multiplexer_4 (
    .in0(4'b0001), .in1(4'b0011), .in2(4'b1111), .out(multiplexer_4_out), .sel(instMem[13:12]));  // open: in3
  not not_15 (not_15_out, comparator_1_eq);
  not not_16 (not_16_out, comparator_2_eq);
  assign WRITE_ENABLE = bit_extender_3_out & multiplexer_4_out;  // AND_Gate and_15, 4 bits wide
  assign bit_extender_4_out = {{1{not_15_out}}, not_15_out};  // Bit_Extender bit_extender_4
  dataHazardSel rs1Hazard (
    .Hazardreg(instID[19:15]), .instEX(instEX), .instMem(instMem), .instWb(instWb), .out_5(rs1Hazard_out_5));
  assign bit_extender_5_out = {{1{not_16_out}}, not_16_out};  // Bit_Extender bit_extender_5
  dataHazardSel rs2Hazrd (
    .Hazardreg(instID[24:20]), .instEX(instEX), .instMem(instMem), .instWb(instWb), .out_5(rs2Hazrd_out_5));
  dataHazardSel raHazard (.Hazardreg(5'b00001), .instEX(instEX), .instMem(instMem), .instWb(instWb), .out_5(raSel));
  dataHazardSel spHazard (.Hazardreg(5'b00010), .instEX(instEX), .instMem(instMem), .instWb(instWb), .out_5(spSel));
  dataHazardSel t0Hazard (.Hazardreg(5'b00101), .instEX(instEX), .instMem(instMem), .instWb(instWb), .out_5(t0Sel));
  assign rs1Sel = bit_extender_4_out & rs1Hazard_out_5;  // AND_Gate and_16, 2 bits wide
  assign rs2Sel = bit_extender_5_out & rs2Hazrd_out_5;  // AND_Gate and_17, 2 bits wide
  Multiplexer #(.enable("false"), .select(3), .width(2)) multiplexer_5 (
    .in0(2'b01), .in1(2'b00), .in3(2'b00), .in6(2'b10), .out(WBSelMem), .sel(instMem[6:4]));  // open: in2, in4, in5, in7
  dataHazardSel t1Hazard (.Hazardreg(5'b00110), .instEX(instEX), .instMem(instMem), .instWb(instWb), .out_5(t1Sel));
  dataHazardSel t2Hazard (.Hazardreg(5'b00111), .instEX(instEX), .instMem(instMem), .instWb(instWb), .out_5(t2Sel));
  dataHazardSel s0Hazard (.Hazardreg(5'b01000), .instEX(instEX), .instMem(instMem), .instWb(instWb), .out_5(s0Sel));
  dataHazardSel s1Hazard (.Hazardreg(5'b01001), .instEX(instEX), .instMem(instMem), .instWb(instWb), .out_5(s1Sel));
  dataHazardSel a0Hazard (.Hazardreg(5'b01010), .instEX(instEX), .instMem(instMem), .instWb(instWb), .out_5(a0Sel));

  assign CSRSel = instID[14];

  // Notes on the sheet:
  //   INPUTS to your circuit
  //   OUTPUT from your circuit
  //   DON'T CHANGE THE LOCATIONS OF THE INPUTS AND OUTPUTS!
endmodule

module dataHazardSel (
  input  [4:0] Hazardreg,
  input  [31:0] instEX,
  input  [31:0] instMem,
  input  [31:0] instWb,
  output [1:0] out_5
);

  wire and_1_out, and_4_out, comparator_1_eq, comparator_2_eq, comparator_3_eq, data_hazard_ex,
       data_hazard_mem, data_hazard_wb, not_1_out, not_2_out, not_3_out, not_4_out, not_5_out, not_6_out,
       not_7_out, not_8_out, not_9_out, not_10_out, or_1_out, or_2_out, or_3_out, or_4_out, or_5_out;
  wire [1:0] rsSel1, rsSel2;

  not not_1 (not_1_out, instEX[0]);
  not not_2 (not_2_out, instEX[1]);
  not not_3 (not_3_out, instMem[0]);
  not not_4 (not_4_out, instMem[1]);
  not not_5 (not_5_out, instMem[4]);
  not not_6 (not_6_out, instMem[5]);
  Multiplexer #(.enable("false"), .select(3), .width(2)) multiplexer_1 (
    .in0(2'b00), .in1(2'b01), .in2(2'b10), .in3(2'b01), .in4(2'b11), .in5(2'b01), .in6(2'b10), .in7(2'b01),
    .out(out_5), .sel({data_hazard_wb, data_hazard_mem, data_hazard_ex}));
  Comparator #(.width(5)) comparator_1 (.a(Hazardreg), .b(instEX[11:7]), .eq(comparator_1_eq));  // open: gt, lt
  or or_1 (or_1_out, not_1_out, not_2_out, instEX[2], instEX[4]);
  Comparator #(.width(5)) comparator_2 (.a(Hazardreg), .b(instMem[11:7]), .eq(comparator_2_eq));  // open: gt, lt
  or or_2 (or_2_out, not_3_out, not_4_out, instMem[2], instMem[4]);
  and and_1 (and_1_out, instMem[0], not_5_out, not_6_out);
  and and_2 (data_hazard_ex, comparator_1_eq, or_1_out);
  or or_3 (or_3_out, or_2_out, and_1_out);
  and and_3 (data_hazard_mem, comparator_2_eq, or_3_out);
  Multiplexer #(.enable("false"), .select(2), .width(2)) multiplexer_2 (
    .in0(2'b00), .in1(2'b01), .in2(2'b10), .in3(2'b01), .out(rsSel1), .sel({data_hazard_mem, data_hazard_ex}));
  Multiplexer #(.enable("false"), .select(2), .width(2)) multiplexer_3 (
    .in0(2'b00), .in1(2'b01), .in2(2'b10), .in3(2'b01), .out(rsSel2), .sel({data_hazard_wb, data_hazard_mem}));
  not not_7 (not_7_out, instWb[0]);
  not not_8 (not_8_out, instWb[1]);
  Comparator #(.width(5)) comparator_3 (.a(Hazardreg), .b(instWb[11:7]), .eq(comparator_3_eq));  // open: gt, lt
  or or_4 (or_4_out, not_7_out, not_8_out, instWb[2], instWb[4]);
  not not_9 (not_9_out, instWb[4]);
  and and_4 (and_4_out, instWb[0], not_9_out, not_10_out);
  not not_10 (not_10_out, instWb[5]);
  or or_5 (or_5_out, or_4_out, and_4_out);
  and and_5 (data_hazard_wb, comparator_3_eq, or_5_out);

  // Other names for the same wires on the sheet: hazard_case[2:0] = {data_hazard_wb, data_hazard_mem, data_hazard_ex};
  //   hazard_case1[1:0] = {data_hazard_mem, data_hazard_ex}; hazard_case2[1:0] = {data_hazard_wb, data_hazard_mem};
  //   rsSel[1:0] = out_5
endmodule
