// Logisim project cpu.circ as structural Verilog: 1 circuit, main circuit cpu
module cpu (
  input  clk,
  input  [31:0] INSTRUCTION,
  input  [31:0] READ_DATA,
  output [31:0] WRITE_ADDRESS,
  output [31:0] PROGRAM_COUNTER,
  output [31:0] ra,
  output [31:0] sp,
  output [31:0] t0,
  output [31:0] t1,
  output [31:0] t2,
  output [31:0] s0,
  output [31:0] s1,
  output [31:0] a0,
  output [31:0] tohost,
  output [3:0] WRITE_ENABLE,
  output [31:0] WRITE_DATA
);

  wire and_1_out, and_2_out, and_3_out, and_4_out, and_5_out, ASel, BrEq, BrLt, BrUn, BSel, CSRSel, CSRWen,
       MemRW, not_1_out, PCSel, PCSelEX, register_4_q, RegWEn;
  wire [1:0] a0Sel, raSel, rs1Sel, rs2Sel, s0Sel, s1Sel, spSel, t0Sel, t1Sel, t2Sel, WBSel, WBSelMem;
  wire [2:0] immSel;
  wire [3:0] ALUSel;
  wire [4:0] register_2_q;
  wire [31:0] a0_read, adder_1_out, adder_2_out, adder_3_out, adder_4_out, adder_5_out, adder_6_out,
       adder_7_out, ALUres, bit_extender_1_out, bit_extender_2_out, imm, INSTRUCTION_EX, INSTRUCTION_IF,
       multiplexer_1_out, multiplexer_4_out, multiplexer_13_out, multiplexer_14_out, multiplexer_18_out,
       multiplexer_19_out, multiplexer_20_out, PC_EX, ra_read, READ_DATA_RES, register_3_q, rs1, rs1_read,
       rs2_read, s0_read, s1_read, sp_read, t0_read, t1_read, t2_read, WB, WBmem;

  Adder #(.width(32)) adder_1 (.a(PROGRAM_COUNTER), .b(32'h4), .out(adder_1_out));  // open: cin, cout
  Multiplexer #(.enable("false"), .width(32)) multiplexer_1 (
    .in0(adder_1_out), .in1(WRITE_ADDRESS), .out(multiplexer_1_out), .sel(PCSel));
  Register #(.width(32)) PC (.D(multiplexer_1_out), .en(1'b1), .clk(clk), .Q(PROGRAM_COUNTER));  // open: clr
  Register #(.width(1)) register_1 (.D(PCSel), .en(1'b1), .clk(clk), .Q(PCSelEX));  // open: clr
  not not_1 (not_1_out, clk);
  Adder #(.width(32)) adder_2 (.a(PC_EX), .b(32'h4), .out(adder_2_out));  // open: cin, cout
  Adder #(.width(32)) adder_3 (.a(PC_EX), .b(32'h4), .out(adder_3_out));  // open: cin, cout
  Register #(.width(5)) register_2 (
    .D(INSTRUCTION_EX[11:7]), .en(1'b1), .clk(not_1_out), .Q(register_2_q));  // open: clr
  Multiplexer #(.enable("false"), .width(32)) multiplexer_2 (
    .in0(WRITE_ADDRESS), .in1(adder_2_out), .sel(and_1_out));  // open: out
  and and_1 (and_1_out, INSTRUCTION_EX[2], INSTRUCTION_EX[6]);
  Multiplexer #(.enable("false"), .width(32)) multiplexer_3 (
    .in0(WRITE_ADDRESS), .in1(adder_3_out), .sel(and_2_out));  // open: out
  and and_2 (and_2_out, INSTRUCTION_EX[2], INSTRUCTION_EX[6]);
  Register #(.width(32)) register_3 (.D(WB), .en(1'b1), .clk(not_1_out), .Q(register_3_q));  // open: clr
  Register #(.width(1)) register_4 (.D(RegWEn), .en(1'b1), .clk(not_1_out), .Q(register_4_q));  // open: clr
  Multiplexer #(.enable("false"), .width(32)) multiplexer_4 (
    .in0(INSTRUCTION), .in1(32'h13), .out(multiplexer_4_out), .sel(PCSel));
  Adder #(.width(32)) adder_4 (.a(PC_EX), .b(32'h4), .out(adder_4_out));  // open: cin, cout
  Adder #(.width(32)) adder_5 (.a(PC_EX), .b(32'h4), .out(adder_5_out));  // open: cin, cout
  Register #(.width(32)) IDreg (.D(multiplexer_4_out), .en(1'b1), .clk(clk), .Q(INSTRUCTION_EX));  // open: clr
  Register #(.width(32)) PCreg1 (.D(PROGRAM_COUNTER), .en(1'b1), .clk(clk), .Q(PC_EX));  // open: clr
  and and_3 (and_3_out, INSTRUCTION_EX[2], INSTRUCTION_EX[6]);
  Multiplexer #(.enable("false"), .select(2), .width(32)) multiplexer_5 (
    .in0(sp_read), .in1(WRITE_ADDRESS), .in2(WBmem), .in3(WB), .sel(spSel));  // open: out
  Multiplexer #(.enable("false"), .select(2), .width(32)) multiplexer_6 (
    .in0(t0_read), .in1(WRITE_ADDRESS), .in2(WBmem), .in3(WB), .sel(t0Sel));  // open: out
  Multiplexer #(.enable("false"), .select(2), .width(32)) multiplexer_7 (
    .in0(t1_read), .in1(WRITE_ADDRESS), .in2(WBmem), .in3(WB), .sel(t1Sel));  // open: out
  Multiplexer #(.enable("false"), .select(2), .width(32)) multiplexer_8 (
    .in0(t2_read), .in1(WRITE_ADDRESS), .in2(WBmem), .in3(WB), .sel(t2Sel));  // open: out
  Multiplexer #(.enable("false"), .select(2), .width(32)) multiplexer_9 (
    .in0(s0_read), .in1(WRITE_ADDRESS), .in2(WBmem), .in3(WB), .sel(s0Sel));  // open: out
  Multiplexer #(.enable("false"), .select(2), .width(32)) multiplexer_10 (
    .in0(s1_read), .in1(WRITE_ADDRESS), .in2(WBmem), .in3(WB), .sel(s1Sel));  // open: out
  Multiplexer #(.enable("false"), .select(2), .width(32)) multiplexer_11 (
    .in0(a0_read), .in1(WRITE_ADDRESS), .in2(WBmem), .in3(WB), .sel(a0Sel));  // open: out
  Multiplexer #(.enable("false"), .select(2), .width(32)) multiplexer_12 (
    .in0(rs2_read), .in1(WRITE_ADDRESS), .in2(WBmem), .in3(WB), .sel(rs2Sel));  // open: out
  Multiplexer #(.enable("false"), .width(32)) multiplexer_13 (
    .in0(WRITE_ADDRESS), .in1(adder_4_out), .out(multiplexer_13_out), .sel(and_3_out));
  Multiplexer #(.enable("false"), .width(32)) multiplexer_14 (
    .in0(WRITE_ADDRESS), .in1(adder_5_out), .out(multiplexer_14_out), .sel(and_4_out));
  and and_4 (and_4_out, INSTRUCTION_EX[2], INSTRUCTION_EX[6]);
  regfile regfile_1 (
    .rs1(INSTRUCTION_EX[19:15]), .rs2(INSTRUCTION_EX[24:20]), .rd(register_2_q), .Write_Data(register_3_q),
    .RegWEn(register_4_q), .clk(clk), .ra(ra), .sp(sp), .t0(t0), .t1(t1), .t2(t2), .s0(s0), .s1(s1), .a0(a0),
    .Read_Data_1(rs1), .Read_Data_2(WRITE_DATA));
  Multiplexer #(.enable("false"), .select(2), .width(32)) multiplexer_15 (
    .in0(ra_read), .in1(multiplexer_13_out), .in2(WBmem), .in3(WB), .sel(raSel));  // open: out
  Multiplexer #(.enable("false"), .select(2), .width(32)) multiplexer_16 (
    .in0(rs1_read), .in1(multiplexer_14_out), .in2(WBmem), .in3(WB), .sel(rs1Sel));  // open: out
  imm_gen imm_gen_1 (.inst(INSTRUCTION_EX), .ImmSel(immSel), .imm(imm));
  Multiplexer #(.enable("false"), .width(32)) multiplexer_17 (.in1(32'h13), .sel(PCSel));  // open: in0, out
  Multiplexer #(.enable("false"), .width(32)) multiplexer_18 (
    .in0(rs1), .in1(imm), .out(multiplexer_18_out), .sel(CSRSel));
  Register #(.width(32)) EXreg (.en(1'b1), .clk(clk));  // open: D, Q, clr
  Register #(.width(32)) PCreg2 (.en(1'b1), .clk(clk));  // open: D, Q, clr
  Register #(.width(32)) rs1reg (.en(1'b1), .clk(clk));  // open: D, Q, clr
  Register #(.width(32)) rs2regEX (.en(1'b1), .clk(clk));  // open: D, Q, clr
  Register #(.width(32)) immreg (.en(1'b1), .clk(clk));  // open: D, Q, clr
  Multiplexer #(.enable("false"), .width(32)) multiplexer_19 (
    .in0(rs1), .in1(PC_EX), .out(multiplexer_19_out), .sel(ASel));
  Multiplexer #(.enable("false"), .width(32)) multiplexer_20 (
    .in0(WRITE_DATA), .in1(imm), .out(multiplexer_20_out), .sel(BSel));
  and and_5 (and_5_out, INSTRUCTION_EX[4], INSTRUCTION_EX[6]);
  control_logic control_logic_1 (
    .BrUn(BrUn), .ASel(ASel), .BSel(BSel), .ALUSel(ALUSel), .MemRW(MemRW), .WRITE_ENABLE(WRITE_ENABLE),
    .WBSel(WBSel), .WBSelMem(WBSelMem), .CSRSel(CSRSel), .CSRWen(CSRWen), .PCSel(PCSel), .RegWEn(RegWEn),
    .ImmSel(immSel), .raSel(raSel), .spSel(spSel), .t0Sel(t0Sel), .t1Sel(t1Sel), .t2Sel(t2Sel),
    .s0Sel(s0Sel), .s1Sel(s1Sel), .a0Sel(a0Sel), .rs1Sel(rs1Sel), .rs2Sel(rs2Sel), .instIF(INSTRUCTION_IF),
    .instID(INSTRUCTION_EX), .instEX(INSTRUCTION_EX), .instMem(INSTRUCTION_EX), .instWb(INSTRUCTION_EX),
    .BrEq(BrEq), .BrLt(BrLt));
  alu alu_1 (.Result(ALUres), .A(multiplexer_19_out), .B(multiplexer_20_out), .ALUSel(ALUSel));  // open: out_5
  Multiplexer #(.enable("false"), .width(32)) multiplexer_21 (
    .in0(ALUres), .in1(tohost), .out(WRITE_ADDRESS), .sel(and_5_out));
  branch_comp branch_comp_1 (.rs1(rs1), .rs2(WRITE_DATA), .BrUn(BrUn), .BrEq(BrEq), .BrLt(BrLt));
  csr csr_1 (
    .CSR_address(INSTRUCTION_EX[31:20]), .CSR_din(multiplexer_18_out), .CSR_WE(CSRWen), .clk(clk),
    .tohost(tohost));
  Register #(.width(32)) Memreg (.en(1'b1), .clk(clk));  // open: D, Q, clr
  Register #(.width(32)) PCreg3 (.en(1'b1), .clk(clk));  // open: D, Q, clr
  Register #(.width(32)) ALUreg1 (.en(1'b1), .clk(clk));  // open: D, Q, clr
  Register #(.width(32)) rs2regMEM (.en(1'b1), .clk(clk));  // open: D, Q, clr
  Adder #(.width(32)) adder_6 (.a(PC_EX), .b(32'h4), .out(adder_6_out));  // open: cin, cout
  assign bit_extender_1_out = {{24{READ_DATA[7]}}, READ_DATA[7:0]};  // Bit_Extender bit_extender_1
  assign bit_extender_2_out = {{16{READ_DATA[15]}}, READ_DATA[15:0]};  // Bit_Extender bit_extender_2
  Multiplexer #(.enable("false"), .select(2), .width(32)) multiplexer_22 (
    .in0(WRITE_ADDRESS), .in1(READ_DATA_RES), .in2(adder_6_out), .out(WBmem), .sel(WBSelMem));  // open: in3
  Multiplexer #(.enable("false"), .select(2), .width(32)) multiplexer_23 (
    .in0(bit_extender_1_out), .in1(bit_extender_2_out), .in2(READ_DATA), .out(READ_DATA_RES),
    .sel(INSTRUCTION_EX[13:12]));  // open: in3
  Register #(.width(32)) PCreg4 (.en(1'b1), .clk(clk));  // open: D, Q, clr
  Register #(.width(32)) ALUreg2 (.en(1'b1), .clk(clk));  // open: D, Q, clr
  Register #(.width(32)) READreg (.en(1'b1), .clk(clk));  // open: D, Q, clr
  Adder #(.width(32)) adder_7 (.a(PC_EX), .b(32'h4), .out(adder_7_out));  // open: cin, cout
  Multiplexer #(.enable("false"), .select(2), .width(32)) multiplexer_24 (
    .in0(WRITE_ADDRESS), .in1(READ_DATA_RES), .in2(adder_7_out), .out(WB), .sel(WBSel));  // open: in3

  // Other names for the same wires on the sheet: ALUmem[31:0] = WRITE_ADDRESS; ALUresult[31:0] = WRITE_ADDRESS;
  //   ALUwb[31:0] = WRITE_ADDRESS; immEX[31:0] = imm; INSTRUCTION_ID[31:0] = INSTRUCTION_EX;
  //   INSTRUCTION_MEM[31:0] = INSTRUCTION_EX; INSTRUCTION_WB[31:0] = INSTRUCTION_EX; PC_ID[31:0] = PC_EX;
  //   PC_MEM[31:0] = PC_EX; PC_WB[31:0] = PC_EX; READ_DATA_WB[31:0] = READ_DATA_RES; rs1EX[31:0] = rs1;
  //   rs2[31:0] = WRITE_DATA; rs2EX[31:0] = WRITE_DATA; rs2MEM[31:0] = WRITE_DATA

  // Notes on the sheet:
  //   Output to IMEM
  //   IMEM (do **NOT** move this)
  //   Inputs from IMEM
  //   Inputs/Outputs for testing. Do **NOT** move these.
  //   Outputs To DMEM
  //   DMEM (do **NOT** move this)
  //   Inputs From DMEM
endmodule
