// Logisim project regfile.circ as structural Verilog: 1 circuit, main circuit regfile
// my_sp
module regfile (
  input  [4:0] rs1,
  input  [4:0] rs2,
  input  [4:0] rd,
  input  [31:0] Write_Data,
  input  RegWEn,
  input  clk,
  output [31:0] ra,
  output [31:0] sp,
  output [31:0] t0,
  output [31:0] t1,
  output [31:0] t2,
  output [31:0] s0,
  output [31:0] s1,
  output [31:0] a0,
  output [31:0] Read_Data_1,
  output [31:0] Read_Data_2
);

  wire en_a0, en_ra, en_s0, en_s1, en_sp, en_t0, en_t1, en_t2, en_x3, en_x4, en_x11, en_x12, en_x13, en_x14,
       en_x15, en_x16, en_x17, en_x18, en_x19, en_x20, en_x21, en_x22, en_x23, en_x24, en_x25, en_x26,
       en_x27, en_x28, en_x29, en_x30, en_x31;
  wire [31:0] wirte_data, write_dara, x0, x3, x4, x11, x12, x13, x14, x15, x16, x17, x18, x19, x20, x21, x22,
       x23, x24, x25, x26, x27, x28, x29, x30, x31;

  Demultiplexer #(.enable("false"), .select(5)) demultiplexer_1 (
    .out1(en_ra), .out2(en_sp), .out3(en_x3), .out4(en_x4), .out5(en_t0), .out6(en_t1), .out7(en_t2),
    .out8(en_s0), .out9(en_s1), .out10(en_a0), .out11(en_x11), .out12(en_x12), .out13(en_x13),
    .out14(en_x14), .out15(en_x15), .out16(en_x16), .out17(en_x17), .out18(en_x18), .out19(en_x19),
    .out20(en_x20), .out21(en_x21), .out22(en_x22), .out23(en_x23), .out24(en_x24), .out25(en_x25),
    .out26(en_x26), .out27(en_x27), .out28(en_x28), .out29(en_x29), .out30(en_x30), .out31(en_x31),
    .in(RegWEn), .sel(rd));  // open: out0
  // NoConnect on nothing
  // NoConnect on nothing
  // NoConnect on nothing
  Register #(.width(32)) my_ra (.D(Write_Data), .en(en_ra), .clk(clk), .Q(ra));  // open: clr
  Register #(.width(32)) my_sp (.D(Write_Data), .en(en_sp), .clk(clk), .Q(sp));  // open: clr
  Register #(.width(32)) my_s0 (.D(Write_Data), .en(en_s0), .clk(clk), .Q(s0));  // open: clr
  Register #(.width(32)) my_s1 (.D(Write_Data), .en(en_s1), .clk(clk), .Q(s1));  // open: clr
  Register #(.width(32)) my_x0 (.D({32{1'b0}}), .en(RegWEn), .clk(clk), .Q(x0));  // open: clr
  Register #(.width(32)) my_x3 (.D(Write_Data), .en(en_x3), .clk(clk), .Q(x3));  // open: clr
  Register #(.width(32)) my_x4 (.D(Write_Data), .en(en_x4), .clk(clk), .Q(x4));  // open: clr
  Register #(.width(32)) my_x11 (.D(Write_Data), .en(en_x11), .clk(clk), .Q(x11));  // open: clr
  Register #(.width(32)) my_x12 (.D(Write_Data), .en(en_x12), .clk(clk), .Q(x12));  // open: clr
  Register #(.width(32)) my_x13 (.D(Write_Data), .en(en_x13), .clk(clk), .Q(x13));  // open: clr
  Register #(.width(32)) my_x14 (.D(Write_Data), .en(en_x14), .clk(clk), .Q(x14));  // open: clr
  Register #(.width(32)) my_x15 (.D(Write_Data), .en(en_x15), .clk(clk), .Q(x15));  // open: clr
  Register #(.width(32)) my_x16 (.D(Write_Data), .en(en_x28), .clk(clk), .Q(x16));  // open: clr
  Register #(.width(32)) my_x17 (.D(Write_Data), .en(en_x17), .clk(clk), .Q(x17));  // open: clr
  Register #(.width(32)) my_x18 (.D(Write_Data), .en(en_x18), .clk(clk), .Q(x18));  // open: clr
  Register #(.width(32)) my_x19 (.D(Write_Data), .en(en_x19), .clk(clk), .Q(x19));  // open: clr
  Register #(.width(32)) my_a0 (.D(Write_Data), .en(en_a0), .clk(clk), .Q(a0));  // open: clr
  Register #(.width(32)) my_t0 (.D(Write_Data), .en(en_t0), .clk(clk), .Q(t0));  // open: clr
  Register #(.width(32)) my_t1 (.D(write_dara), .en(en_t1), .clk(clk), .Q(t1));  // open: clr
  Register #(.width(32)) my_t2 (.D(Write_Data), .en(en_t2), .clk(clk), .Q(t2));  // open: clr
  Register #(.width(32)) my_x20 (.D(Write_Data), .en(en_x20), .clk(clk), .Q(x20));  // open: clr
  Register #(.width(32)) my_x21 (.D(Write_Data), .en(en_x21), .clk(clk), .Q(x21));  // open: clr
  Register #(.width(32)) my_x22 (.D(wirte_data), .en(en_x22), .clk(clk), .Q(x22));  // open: clr
  Register #(.width(32)) my_x23 (.D(Write_Data), .en(en_x23), .clk(clk), .Q(x23));  // open: clr
  Register #(.width(32)) my_x24 (.D(Write_Data), .en(en_x24), .clk(clk), .Q(x24));  // open: clr
  Register #(.width(32)) my_x25 (.D(Write_Data), .en(en_x25), .clk(clk), .Q(x25));  // open: clr
  Register #(.width(32)) my_x26 (.D(Write_Data), .en(en_x26), .clk(clk), .Q(x26));  // open: clr
  Register #(.width(32)) my_x27 (.D(Write_Data), .en(en_x27), .clk(clk), .Q(x27));  // open: clr
  Register #(.width(32)) my_x28 (.D(Write_Data), .en(en_x28), .clk(clk), .Q(x28));  // open: clr
  Register #(.width(32)) my_x29 (.D(Write_Data), .en(en_x29), .clk(clk), .Q(x29));  // open: clr
  Register #(.width(32)) my_x30 (.D(Write_Data), .en(en_x30), .clk(clk), .Q(x30));  // open: clr
  Register #(.width(32)) my_x31 (.D(Write_Data), .en(en_x31), .clk(clk), .Q(x31));  // open: clr
  Multiplexer #(.enable("false"), .select(5), .width(32)) multiplexer_1 (
    .in0(x0), .in1(ra), .in2(sp), .in3(x3), .in4(x4), .in5(t0), .in6(t1), .in7(t2), .in8(s0), .in9(s1),
    .in10(a0), .in11(x11), .in12(x12), .in13(x13), .in14(x14), .in15(x15), .in16(x16), .in17(x17),
    .in18(x18), .in19(x19), .in20(x20), .in21(x21), .in22(x22), .in23(x23), .in24(x24), .in25(x25),
    .in26(x26), .in27(x27), .in28(x28), .in29(x29), .in30(x30), .in31(x31), .out(Read_Data_1), .sel(rs1));
  Multiplexer #(.enable("false"), .select(5), .width(32)) multiplexer_2 (
    .in0(x0), .in1(ra), .in2(sp), .in3(x3), .in4(x4), .in5(t0), .in6(t1), .in7(t2), .in8(s0), .in9(s1),
    .in10(a0), .in11(x11), .in12(x12), .in13(x13), .in14(x14), .in15(x15), .in16(x16), .in17(x17),
    .in18(x18), .in19(x19), .in20(x20), .in21(x21), .in22(x22), .in23(x23), .in24(x24), .in25(x25),
    .in26(x26), .in27(x27), .in28(x28), .in29(x29), .in30(x30), .in31(x31), .out(Read_Data_2), .sel(rs2));

  // Other names for the same wires on the sheet: read_data1[31:0] = Read_Data_1; read_data2[31:0] = Read_Data_2;
  //   read_reg1[4:0] = rs1; read_reg2[4:0] = rs2; write_en = RegWEn; write_reg[4:0] = rd

  // Notes on the sheet:
  //   INPUTS to your circuit
  //   DON'T CHANGE THE LOCATIONS OF THE INPUTS AND OUTPUTS!
  //   These are DEBUG/TEST outputs from your circuit.
  //   OUTPUTS from your circuit
endmodule
